# Fritzing sketch Pixi Placer Mainboard (saved by Fritzing 1.0.5)
circuit board: 11.552cm x 5.92382cm
breadboards: 1

parts:
  Pico_W = Raspberry Pi Pico W
  TMC_2208_X_axis = Pololu A4988 [package=SO16]
  TMC_2208_Y_axis = Pololu A4988 [package=SO16]
  TMC_2208_Head = Pololu A4988 [package=SO16]
  J1 = female pin header, 20 pins [form="♀ (female)"]
  LM2596 = LM2596 step down module
  12v = Power plug
  J3 = double row female pin header, 32 pins [form="♀ (female)"]
  J2 = double row female pin header, 40 pins [form="♀ (female)"]
  F1 = Resettable Fuse PTC 1812 [package=ptc-1812]
  F2 = Resettable Fuse PTC 1812 [package=ptc-1812]
  F3 = Resettable Fuse PTC 1812 [package=ptc-1812]
  D1 = Schottky Diode [part_number=1N5817 package="300 mil [THT]"]

nets:
  N1: Pico_W.pin_1, J1.pin1
  N2: Pico_W.pin_2, J1.pin2
  N3: Pico_W.pin_3, Pico_W.pin_8, Pico_W.pin_13, Pico_W.pin_18, Pico_W.pin_23, Pico_W.pin_28, Pico_W.pin_33, Pico_W.pin_38, TMC_2208_X_axis.GND#8, TMC_2208_Y_axis.GND#8, TMC_2208_Head.GND#8, J1.pin3, J1.pin8, J1.pin13, J1.pin18, LM2596.OUT-, J2.pin1, J2.pin2, J2.pin3, J2.pin4, J2.pin5, J2.pin6, J2.pin7, J2.pin8, J2.pin9, J2.pin10, J2.pin11, J2.pin12, J2.pin13, J2.pin14, J2.pin15, J2.pin16, J2.pin17, J2.pin18, J2.pin19, J2.pin20, J2.pin23, J2.pin28, J2.pin33, J2.pin38
  N4: Pico_W.pin_4, J1.pin4
  N5: Pico_W.pin_5, TMC_2208_X_axis.STEP, J1.pin5
  N6: Pico_W.pin_6, TMC_2208_X_axis.ENABLE, J1.pin6
  N7: Pico_W.pin_7, TMC_2208_X_axis.DIR, J1.pin7
  N8: Pico_W.pin_9, TMC_2208_Y_axis.DIR, J1.pin9
  N9: Pico_W.pin_10, TMC_2208_Y_axis.ENABLE, J1.pin10
  N10: Pico_W.pin_11, TMC_2208_Y_axis.STEP, J1.pin11
  N11: Pico_W.pin_12, J1.pin12
  N12: Pico_W.pin_14, TMC_2208_Head.DIR, J1.pin14
  N13: Pico_W.pin_15, TMC_2208_Head.STEP, J1.pin15
  N14: Pico_W.pin_16, TMC_2208_Head.ENABLE, J1.pin16
  N15: Pico_W.pin_17, J1.pin17
  N16: Pico_W.pin_19, J1.pin19
  N17: Pico_W.pin_20, J1.pin20
  N18: Pico_W.pin_21, J2.pin21
  N19: Pico_W.pin_22, J2.pin22
  N20: Pico_W.pin_24, J2.pin24
  N21: Pico_W.pin_25, J2.pin25
  N22: Pico_W.pin_26, J2.pin26
  N23: Pico_W.pin_27, J2.pin27
  N24: Pico_W.pin_29, J2.pin29
  N25: Pico_W.pin_30, J2.pin30
  N26: Pico_W.pin_31, J2.pin31
  N27: Pico_W.pin_32, J2.pin32
  N28: Pico_W.pin_34, J2.pin34
  N29: Pico_W.pin_35, J2.pin35
  VDD: Pico_W.pin_36, TMC_2208_X_axis.VDD, TMC_2208_Y_axis.VDD, TMC_2208_Head.VDD, J2.pin36
  N30: Pico_W.pin_37, J2.pin37
  N31: Pico_W.pin_39, J2.pin39, D1.cathode
  N32: Pico_W.pin_40, J2.pin40
  N33: TMC_2208_X_axis.1B, J3.pin9, J3.pin24
  N34: TMC_2208_X_axis.1A, J3.pin10, J3.pin23
  N35: TMC_2208_X_axis.2A, J3.pin11, J3.pin22
  N36: TMC_2208_X_axis.2B, J3.pin12, J3.pin21
  N37: TMC_2208_X_axis.GND#14, TMC_2208_Y_axis.GND#14, TMC_2208_Head.GND#14, LM2596.IN-, 12v.GND, J3.pin17, J3.pin18, J3.pin19, J3.pin20
  N38: TMC_2208_X_axis.VMOT, TMC_2208_Y_axis.VMOT, TMC_2208_Head.VMOT, F1.1
  N39: TMC_2208_Y_axis.1B, J3.pin8, J3.pin25
  N40: TMC_2208_Y_axis.1A, J3.pin7, J3.pin26
  N41: TMC_2208_Y_axis.2A, J3.pin6, J3.pin27
  N42: TMC_2208_Y_axis.2B, J3.pin5, J3.pin28
  N43: TMC_2208_Head.1B, J3.pin1, J3.pin32
  N44: TMC_2208_Head.1A, J3.pin2, J3.pin31
  N45: TMC_2208_Head.2A, J3.pin3, J3.pin30
  N46: TMC_2208_Head.2B, J3.pin4, J3.pin29
  N47: LM2596.IN+, F2.1
  N48: LM2596.OUT+, J3.pin13, J3.pin14, D1.anode
  N49: 12v.VCC, F1.2, F2.2, F3.2
  N50: J3.pin15, J3.pin16, F3.1

notes:
  H E A D
  Y Axis
  X Axis
  GND   GND    GND    GND   GND    GND
  GND GND
  5v
  12v
  Pixi Placer v0.1

custom parts:
  Raspberry Pi Pico W: Raspberry Pi Pico W. Based around the RP2040 microcontroller the Pico W is a low cost microcontroller device bringing Raspberry Pi quality, cost, and easy of use to the microcontroller space. The areas marked KEEPOUT in pcb silkscreen should not have traces running through them to avoid shorts on a soldered in module!
  LM2596 step down module: LM2596 DC-DC step down power supply module 3 A.
  Power plug: power plug
  Resettable Fuse PTC 1812: Resettable Fuse PTC Resettable Fuse.
